# Fritzing sketch esp_led_lights (saved by Fritzing 0.9.3b)
breadboards: 1

parts:
  Part1 = Breadboard Power Supply Board SMD
  Part2 = Arduino Uno (Rev3)
  U1 = ESP8266 WiFi Module [part_number=ESP8266]
  R1 = Resistor [tolerance=±1% resistance=1k package=THT]
  R2 = Resistor [tolerance=±1% resistance=1k package=THT]
  S1 = Momentary Switch [package=ksa_sealed_tac_switch]
  R3 = Resistor [tolerance=±1% resistance=10 package=THT]
  H1 = polarizedheader 4pin 0.156in [package=THT]
  Q1 = Basic FET N-Channel [package="TO220 [THT]"]
  Q2 = Basic FET N-Channel [package="TO220 [THT]"]
  Q3 = Basic FET N-Channel [package="TO220 [THT]"]
  J1 = Power Jack [package=power_jack_pth]

nets:
  GND: Part1.GND, Part2.GND, U1.GND, R1.Pin_1, S1.2, R3.Pin_0, Q1.source, Q2.source, Q3.source, J1.GND
  VCC: Part1.VCC, U1.VCC, U1.CH_PD
  N1: Part2.D9_PWM, Q1.gate
  N2: Part2.D10_PWM/SS, Q2.gate
  N3: Part2.D11_PWM/MOSI, Q3.gate
  N4: Part2.D6_PWM, U1.TXD
  N5: Part2.D7, R2.Pin_0
  N6: U1.RXD, R1.Pin_0, R2.Pin_1
  N7: U1.RST, S1.3
  N8: H1.pin1, Q1.drain
  N9: H1.pin2, Q2.drain
  N10: H1.pin3, Q3.drain
  N11: H1.pin4, J1.PWR

custom parts:
  ESP8266 WiFi Module: Generic WiFi Module based on the ESP8266 with onboard PCB antenna and UART communications
